# Fritzing sketch pythonShutdownWiring (saved by Fritzing 0.9.3b)

parts:
  Raspberry_Pi_1 = Raspberry Pi 3 [part_number=RPI-3-V1.2]
  LED1 = LED - 5mm [color="Red (633nm)" package="5 mm [THT]"]
  S1 = Pushbutton [package="[THT]"]
  R1 = Resistor [tolerance=±5% resistance=330 package=THT]

nets:
  N1: Raspberry_Pi_1.GND, S1.Pin_3, S1.Pin_4, R1.Pin_1
  N2: Raspberry_Pi_1.GIPO21, S1.Pin_1, S1.Pin_2
  N3: Raspberry_Pi_1.GIPO16, LED1.anode
  N4: LED1.cathode, R1.Pin_0
